// Logisim project alu.circ as structural Verilog: 1 circuit, main circuit alu
module alu (
  input  [31:0] A,
  input  [31:0] B,
  input  [3:0] ALUSel,
  output [31:0] Result
);

  wire [0:0] sltt;
  wire [31:0] add0, andd, mulh, mulhu, mull, orrr, slll, sraa, srll, subb, xorr;

  Multiplexer #(.enable("false"), .select(4), .width(32)) multiplexer_1 (
    .in0(add0), .in1(slll), .in2({{31{1'b0}}, sltt[0]}), .in4(xorr), .in5(srll), .in6(orrr), .in7(andd),
    .in8(mull), .in9(mulh), .in11(mulhu), .in12(subb), .in13(sraa), .in15(B), .out(Result), .sel(ALUSel));  // open: in3, in10, in14
  Comparator #(.width(32)) comparator_1 (.a(A), .b(B), .lt(sltt[0]));  // open: gt, eq
  Adder #(.width(32)) adder_1 (.a(A), .b(B), .out(add0));  // open: cin, cout
  Shifter #(.width(32)) shifter_1 (.in(A), .\dist (B[4:0]), .out(slll));
  Shifter #(.shift("lr"), .width(32)) shifter_2 (.in(A), .\dist (B[4:0]), .out(srll));
  assign xorr = A ^ B;  // XOR_Gate xor_1, 32 bits wide
  assign orrr = A | B;  // OR_Gate or_1, 32 bits wide
  assign andd = A & B;  // AND_Gate and_1, 32 bits wide
  Shifter #(.shift("ar"), .width(32)) shifter_3 (.in(A), .\dist (B[4:0]), .out(sraa));
  Multiplier #(.mode("twosComplement"), .width(32)) multiplier_1 (.a(A), .b(B), .out(mull), .cout(mulh));  // open: cin
  Subtractor #(.width(32)) subtractor_1 (.a(A), .b(B), .out(subb));  // open: bin, bout
  Multiplier #(.width(32)) multiplier_2 (.a(A), .b(B), .cout(mulhu));  // open: out, cin

  // Notes on the sheet:
  //   INPUTS to your circuit
  //   DON'T CHANGE THE LOCATIONS OF THE INPUTS AND OUTPUTS!
  //   OUTPUT from your circuit
endmodule
