// Logisim project control-logic.circ as structural Verilog: 1 circuit, main circuit control_logic
module control_logic (
  input  [31:0] inst,
  input  BrEq,
  input  BrLt,
  output PCSel,
  output RegWEn,
  output [2:0] ImmSel,
  output BrUn,
  output ASel,
  output BSel,
  output [3:0] ALUSel,
  output MemRW,
  output [1:0] WBSel,
  output CSRSel,
  output CSRWen
);

  wire and_1_out, and_2_out, and_3_out, and_4_out, demultiplexer_1_out0, demultiplexer_1_out1,
       demultiplexer_2_out0, demultiplexer_2_out1, demultiplexer_3_out0, demultiplexer_3_out1,
       demultiplexer_4_out13, demultiplexer_6_out0, demultiplexer_7_out1, demultiplexer_8_out1, not_1_out,
       not_2_out, not_3_out, or_1_out, priority_encoder_2_gs, ROM_I2, ROM_UJ, TYPE_CSR, TYPE_I, TYPE_R,
       TYPE_S, TYPE_SB, TYPE_U, xor_1_out, xor_2_out;
  wire [1:0] ROM_CSR, ROM_U;
  wire [2:0] priority_encoder_2_out, ROM_S;
  wire [4:0] priority_encoder_1_out;
  wire [5:0] adder_1_out, ROM_IN, ROM_SB;
  wire [10:0] ROM_I;
  wire [11:0] ROM_R;

  Demultiplexer #(.enable("false")) demultiplexer_1 (
    .out0(demultiplexer_1_out0), .out1(demultiplexer_1_out1), .in(TYPE_R), .sel(inst[14]));
  Demultiplexer #(.enable("false")) demultiplexer_2 (
    .out0(demultiplexer_2_out0), .out1(demultiplexer_2_out1), .in(demultiplexer_1_out0), .sel(inst[12]));
  Demultiplexer #(.enable("false")) demultiplexer_3 (
    .out0(demultiplexer_3_out0), .out1(demultiplexer_3_out1), .in(demultiplexer_1_out1), .sel(inst[13]));
  Demultiplexer #(.enable("false"), .select(4)) demultiplexer_4 (
    .out0(ROM_I[0]), .out1(ROM_I[1]), .out2(ROM_I[2]), .out8(ROM_I[3]), .out9(ROM_I[4]), .out10(ROM_I[5]),
    .out12(ROM_I[6]), .out13(demultiplexer_4_out13), .out14(ROM_I[9]), .out15(ROM_I[10]), .in(TYPE_I),
    .sel({inst[4], inst[14:12]}));  // open: out3, out4, out5, out6, out7, out11
  Demultiplexer #(.enable("false"), .select(3)) demultiplexer_5 (
    .out0(ROM_SB[0]), .out1(ROM_SB[1]), .out4(ROM_SB[2]), .out5(ROM_SB[3]), .out6(ROM_SB[4]),
    .out7(ROM_SB[5]), .in(TYPE_SB), .sel(inst[14:12]));  // open: out2, out3
  Demultiplexer #(.enable("false")) demultiplexer_6 (
    .out0(demultiplexer_6_out0), .out1(ROM_R[6]), .in(demultiplexer_2_out0), .sel(inst[13]));
  Demultiplexer #(.enable("false")) demultiplexer_7 (
    .out0(ROM_R[3]), .out1(demultiplexer_7_out1), .in(demultiplexer_2_out1), .sel(inst[25]));
  Demultiplexer #(.enable("false")) demultiplexer_8 (
    .out0(ROM_R[7]), .out1(demultiplexer_8_out1), .in(demultiplexer_3_out0), .sel(inst[12]));
  Demultiplexer #(.enable("false")) demultiplexer_9 (
    .out0(ROM_R[10]), .out1(ROM_R[11]), .in(demultiplexer_3_out1), .sel(inst[12]));
  ROM #(.addrWidth(6), .dataWidth(16)) rom_1 (
    .addr(ROM_IN), .data({RegWEn, ImmSel, BrUn, ASel, BSel, ALUSel, MemRW, WBSel, CSRSel, CSRWen}));
  Demultiplexer #(.enable("false")) demultiplexer_10 (
    .out0(ROM_R[4]), .out1(ROM_R[5]), .in(demultiplexer_7_out1), .sel(inst[13]));
  Demultiplexer #(.enable("false")) demultiplexer_11 (
    .out0(ROM_R[8]), .out1(ROM_R[9]), .in(demultiplexer_8_out1), .sel(inst[30]));
  Demultiplexer #(.enable("false")) demultiplexer_12 (
    .out0(ROM_I[7]), .out1(ROM_I[8]), .in(demultiplexer_4_out13), .sel(inst[30]));
  Demultiplexer #(.enable("false"), .select(2)) demultiplexer_13 (
    .out0(ROM_S[0]), .out1(ROM_S[1]), .out2(ROM_S[2]), .in(TYPE_S), .sel(inst[30:29]));  // open: out3
  Demultiplexer #(.enable("false"), .select(2)) demultiplexer_14 (
    .out0(ROM_R[0]), .out1(ROM_R[1]), .out2(ROM_R[2]), .in(demultiplexer_6_out0), .sel({inst[30], inst[25]}));  // open: out3
  Demultiplexer #(.enable("false")) demultiplexer_15 (.out0(ROM_U[0]), .out1(ROM_U[1]), .in(TYPE_U), .sel(inst[5]));
  Demultiplexer #(.enable("false")) demultiplexer_16 (
    .out0(ROM_CSR[0]), .out1(ROM_CSR[1]), .in(TYPE_CSR), .sel(inst[14]));
  not not_1 (not_1_out, inst[14]);
  not not_2 (not_2_out, inst[13]);
  and and_1 (and_1_out, not_1_out, not_2_out);
  xor xor_1 (xor_1_out, inst[12], BrEq);
  xor xor_2 (xor_2_out, inst[12], BrLt);
  not not_3 (not_3_out, inst[4]);
  and and_2 (and_2_out, and_1_out, xor_1_out);
  and and_3 (and_3_out, inst[14], xor_2_out);
  and and_4 (and_4_out, inst[6], not_3_out);
  or or_1 (or_1_out, inst[2], and_2_out, and_3_out);
  Priority_Encoder #(.select(5)) priority_encoder_1 (
    .in0(ROM_R[0]), .in1(ROM_R[1]), .in2(ROM_R[2]), .in3(ROM_R[3]), .in4(ROM_R[4]), .in5(ROM_R[5]),
    .in6(ROM_R[6]), .in7(ROM_R[7]), .in8(ROM_R[8]), .in9(ROM_R[9]), .in10(ROM_R[10]), .in11(ROM_R[11]),
    .in12(ROM_I[0]), .in13(ROM_I[1]), .in14(ROM_I[2]), .in15(ROM_I[3]), .in16(ROM_I[4]), .in17(ROM_I[5]),
    .in18(ROM_I[6]), .in19(ROM_I[7]), .in20(ROM_I[8]), .in21(ROM_I[9]), .in22(ROM_I[10]), .in23(ROM_S[0]),
    .in24(ROM_S[1]), .in25(ROM_S[2]), .in26(ROM_SB[0]), .in27(ROM_SB[1]), .in28(ROM_SB[2]), .in29(ROM_SB[3]),
    .in30(ROM_SB[4]), .in31(ROM_SB[5]), .out(priority_encoder_1_out), .en_in(1'b1));  // open: gs, en_out
  Priority_Encoder priority_encoder_2 (
    .in0(ROM_U[0]), .in1(ROM_U[1]), .in2(ROM_UJ), .in3(ROM_I2), .in4(ROM_CSR[0]), .in5(ROM_CSR[1]),
    .out(priority_encoder_2_out), .en_in(1'b1), .gs(priority_encoder_2_gs));  // open: in6, in7, en_out
  and and_5 (PCSel, and_4_out, or_1_out);
  Adder #(.width(6)) adder_1 (
    .a({3'b000, priority_encoder_2_out}), .b(6'b100000), .out(adder_1_out));  // open: cin, cout
  Multiplexer #(.enable("false"), .width(6)) multiplexer_1 (
    .in0({1'b0, priority_encoder_1_out}), .in1(adder_1_out), .out(ROM_IN), .sel(priority_encoder_2_gs));
  and and_6 (TYPE_R, ~inst[6], inst[5], inst[4], ~inst[3], ~inst[2], inst[1], inst[0]);  // AND_Gate
  and and_7 (TYPE_I, ~inst[6], ~inst[5], 1'b1, ~inst[3], ~inst[2], inst[1], inst[0]);  // AND_Gate
  and and_8 (TYPE_S, ~inst[6], inst[5], ~inst[4], ~inst[3], ~inst[2], inst[1], inst[0]);  // AND_Gate
  and and_9 (TYPE_SB, inst[6], inst[5], ~inst[4], ~inst[3], ~inst[2], inst[1], inst[0]);  // AND_Gate
  and and_10 (TYPE_U, ~inst[6], 1'b1, inst[4], ~inst[3], inst[2], inst[1], inst[0]);  // AND_Gate
  and and_11 (ROM_UJ, inst[6], inst[5], ~inst[4], inst[3], inst[2], inst[1], inst[0]);  // AND_Gate
  and and_12 (ROM_I2, inst[6], inst[5], ~inst[4], ~inst[3], inst[2], inst[1], inst[0]);  // AND_Gate
  and and_13 (TYPE_CSR, inst[6], inst[5], inst[4], ~inst[3], ~inst[2], inst[1], inst[0]);  // AND_Gate

  // Other names for the same wires on the sheet: OP7 = inst[0]; OP6 = inst[1]; OP5 = inst[2]; OP4 = inst[3];
  //   OP3 = inst[4]; OP2 = inst[5]; OP1 = inst[6]; f3_3 = inst[12]; f3_2 = inst[13]; f3_1 = inst[14]; f7_7 = inst[25];
  //   f7_6 = inst[26]; f7_5 = inst[27]; f7_4 = inst[28]; f7_3 = inst[29]; f7_2 = inst[30]; f7_1 = inst[31];
  //   TYPE_I2 = ROM_I2; TYPE_UJ = ROM_UJ

  // Notes on the sheet:
  //   INPUTS to your circuit
  //   Connect ROM Input here ->
  //   contents of rom_1 (hex, n*v repeats v):
  //   8004 8104 8184 8024 8124 8164 8044 8084 80a4 81a4 80c4 80e4 8200 8200 8200 8204 8224 8244 8284 82a4
  //   83a4 82c4 82e4 1210 1210 1210 2e08 2e08 2608 2608 2e08 2e08 b604 b7e4 c608 8208 5209 500b
  //   ROM FOR CONTROL LOGIC
  //   12
  //   23
  //   26
  //   32
  //   36
  //   DON'T CHANGE THE LOCATIONS OF THE INPUTS AND OUTPUTS!
  //   OUTPUT from your circuit
  //   Reminder: Use combinational logic for PCSel
endmodule
