// Logisim project cpu.circ as structural Verilog: 1 circuit, main circuit cpu
module cpu (
  input  clk,
  input  [31:0] INSTRUCTION,
  input  [31:0] MEM_READ_DATA,
  output [31:0] MEM_WRITE_ADDRESS,
  output [31:0] PROGRAM_COUNTER,
  output [31:0] ra,
  output [31:0] sp,
  output [31:0] t0,
  output [31:0] t1,
  output [31:0] t2,
  output [31:0] s0,
  output [31:0] s1,
  output [31:0] a0,
  output [31:0] tohost,
  output [3:0] MEM_WRITE_ENABLE,
  output [31:0] MEM_WRITE_DATA
);

  wire ASel, BrEq, BrLt, BrUn, BSel, CSRSel, CSRWen, f3_1, f3_2, f3_3, f7_1, f7_2, f7_3, f7_4, f7_5, f7_6,
       f7_7, MemRW, PCSel, RegWEn;
  wire [1:0] WBSel;
  wire [2:0] ImmSel;
  wire [3:0] ALUSel, multiplexer_11_out;
  wire [24:0] INSTRUCTION_t;
  wire [31:0] adder_1_out, adder_2_out, bit_extender_1_out, bit_extender_2_out, bit_extender_3_out,
       bit_extender_4_out, bit_extender_5_out, bit_extender_6_out, CSR_in, imm, mem_to_reg,
       multiplexer_1_out, multiplexer_2_out, multiplexer_4_out, multiplexer_5_out, multiplexer_6_out,
       multiplexer_7_out, PC, RD1, RD2, wb;

  Adder #(.width(32)) adder_1 (.a(PROGRAM_COUNTER), .b(32'h4), .out(adder_1_out));  // open: cin, cout
  Register #(.width(32)) u_PC (.D(multiplexer_1_out), .clk(clk), .Q(PROGRAM_COUNTER));  // open: en, clr
  Multiplexer #(.enable("false"), .width(32)) multiplexer_1 (
    .in0(adder_1_out), .in1(MEM_WRITE_ADDRESS), .out(multiplexer_1_out), .sel(PCSel));
  Multiplexer #(.enable("false"), .width(32)) multiplexer_2 (
    .in0(INSTRUCTION), .in1(32'h13), .out(multiplexer_2_out), .sel(PCSel));
  Register #(.width(32)) register_1 (
    .D(multiplexer_2_out), .clk(clk),
    .Q({f7_1, f7_2, f7_3, f7_4, f7_5, f7_6, f7_7, INSTRUCTION_t[24:15], f3_1, f3_2, f3_3, INSTRUCTION_t[11:0]}));  // open: en, clr
  control_logic control_logic_1 (
    .CSRWen(CSRWen), .PCSel(PCSel), .RegWEn(RegWEn), .ImmSel(ImmSel), .BrUn(BrUn), .ASel(ASel), .BSel(BSel),
    .ALUSel(ALUSel), .MemRW(MemRW), .WBSel(WBSel), .CSRSel(CSRSel),
    .inst({f7_1, f7_2, f7_3, f7_4, f7_5, f7_6, f7_7, INSTRUCTION_t[24:15], f3_1, f3_2, f3_3, INSTRUCTION_t[11:0]}),
    .BrEq(BrEq), .BrLt(BrLt));
  imm_gen imm_gen_1 (
    .inst({f7_1, f7_2, f7_3, f7_4, f7_5, f7_6, f7_7, INSTRUCTION_t[24:15], f3_1, f3_2, f3_3, INSTRUCTION_t[11:0]}),
    .ImmSel(ImmSel), .imm(imm));
  Multiplexer #(.enable("false"), .width(32)) multiplexer_3 (.in0(RD1), .in1(imm), .out(CSR_in), .sel(CSRSel));
  regfile regfile_1 (
    .rs1(INSTRUCTION_t[19:15]), .rs2(INSTRUCTION_t[24:20]), .rd(INSTRUCTION_t[11:7]), .Write_Data(wb),
    .RegWEn(RegWEn), .clk(clk), .ra(ra), .sp(sp), .t0(t0), .t1(t1), .t2(t2), .s0(s0), .s1(s1), .a0(a0),
    .Read_Data_1(RD1), .Read_Data_2(RD2));
  branch_comp branch_comp_1 (.rs1(RD1), .rs2(RD2), .BrUn(BrUn), .BrEq(BrEq), .BrLt(BrLt));
  Multiplexer #(.enable("false"), .width(32)) multiplexer_4 (.in0(RD1), .in1(PC), .out(multiplexer_4_out), .sel(ASel));
  Multiplexer #(.enable("false"), .width(32)) multiplexer_5 (.in0(RD2), .in1(imm), .out(multiplexer_5_out), .sel(BSel));
  alu alu_1 (.Result(MEM_WRITE_ADDRESS), .A(multiplexer_4_out), .B(multiplexer_5_out), .ALUSel(ALUSel));
  // csr csr_1: pin names not known; wires that end beside it: 12'h51e, CSR_in, CSRWen, clk, tohost
  Register #(.width(32)) register_2 (.D(PROGRAM_COUNTER), .clk(clk), .Q(PC));  // open: en, clr
  assign bit_extender_1_out = {{24{MEM_READ_DATA[7]}}, MEM_READ_DATA[7:0]};  // Bit_Extender bit_extender_1
  assign bit_extender_2_out = {{24{MEM_READ_DATA[15]}}, MEM_READ_DATA[15:8]};  // Bit_Extender bit_extender_2
  assign bit_extender_3_out = {{24{MEM_READ_DATA[23]}}, MEM_READ_DATA[23:16]};  // Bit_Extender bit_extender_3
  assign bit_extender_4_out = {{24{MEM_READ_DATA[31]}}, MEM_READ_DATA[31:24]};  // Bit_Extender bit_extender_4
  assign bit_extender_5_out = {{16{MEM_READ_DATA[15]}}, MEM_READ_DATA[15:0]};  // Bit_Extender bit_extender_5
  assign bit_extender_6_out = {{16{MEM_READ_DATA[31]}}, MEM_READ_DATA[31:16]};  // Bit_Extender bit_extender_6
  Multiplexer #(.enable("false"), .select(2), .width(32)) multiplexer_6 (
    .in0(bit_extender_1_out), .in1(bit_extender_2_out), .in2(bit_extender_3_out), .in3(bit_extender_4_out),
    .out(multiplexer_6_out), .sel(imm[1:0]));
  Multiplexer #(.enable("false"), .select(2), .width(32)) multiplexer_7 (
    .in0(bit_extender_5_out), .in2(bit_extender_6_out), .out(multiplexer_7_out), .sel(imm[1:0]));  // open: in1, in3
  Adder #(.width(32)) adder_2 (.a(PC), .b(32'h4), .out(adder_2_out));  // open: cin, cout
  Multiplexer #(.enable("false"), .select(2), .width(32)) multiplexer_8 (
    .in0(multiplexer_6_out), .in1(multiplexer_7_out), .in2(MEM_READ_DATA), .out(mem_to_reg),
    .sel({f3_2, f3_3}));  // open: in3
  Multiplexer #(.enable("false"), .select(2), .width(32)) multiplexer_9 (
    .in0(mem_to_reg), .in1(MEM_WRITE_ADDRESS), .in2(adder_2_out), .out(wb), .sel(WBSel));  // open: in3
  Multiplexer #(.enable("false"), .select(4), .width(32)) multiplexer_10 (
    .in0({RD2[7:0], {24{1'b0}}}), .in1({{8{1'b0}}, RD2[7:0], {16{1'b0}}}),
    .in2({{16{1'b0}}, RD2[7:0], {8{1'b0}}}), .in3({{24{1'b0}}, RD2[7:0]}), .in4({{16{1'b0}}, RD2[15:0]}),
    .in6({RD2[15:0], {16{1'b0}}}), .in8(RD2), .out(MEM_WRITE_DATA), .sel({f3_2, f3_3, imm[1:0]}));  // open: in5, in7, in9, in10, in11, in12, in13, in14, in15
  Multiplexer #(.enable("false"), .select(4), .width(4)) multiplexer_11 (
    .in0(4'b0000), .in1(4'b0010), .in2(4'b0100), .in3(4'b1000), .in4(4'b0011), .in6(4'b1100), .in8(4'b1111),
    .out(multiplexer_11_out), .sel({f3_2, f3_3, imm[1:0]}));  // open: in5, in7, in9, in10, in11, in12, in13, in14, in15
  Multiplexer #(.enable("false"), .width(4)) multiplexer_12 (
    .in0(4'b0000), .in1(multiplexer_11_out), .out(MEM_WRITE_ENABLE), .sel(MemRW));

  // Other names for the same wires on the sheet: RD2_7[7:0] = RD2[7:0]; last2digits[1:0] = imm[1:0];
  //   INSTRUCTION_t (some bits) = {f7_1, f7_2, f7_3, f7_4, f7_5, f7_6, f7_7, f3_1, f3_2, f3_3};
  //   alu_result[31:0] = MEM_WRITE_ADDRESS; rd[4:0] = INSTRUCTION_t[11:7]; rs1[4:0] = INSTRUCTION_t[19:15];
  //   rs2[4:0] = INSTRUCTION_t[24:20]; PC_0[31:0] = PROGRAM_COUNTER; real_instr[31:0] = INSTRUCTION

  // Notes on the sheet:
  //   Output to IMEM
  //   IMEM (do **NOT** move this)
  //   Inputs from IMEM
  //   It is OK to move the PC, RegFile, ALU, MEM, Branch Comp, Imm Gen, and Control Logic to wherever is most convenient for you when constructing your CPU, and to delete this text
  //   Inputs/Outputs for testing. Do **NOT** move these.
  //   Outputs To DMEM
  //   DMEM (do **NOT** move this)
  //   Inputs From DMEM
endmodule
