// Logisim project imm-gen.circ as structural Verilog: 1 circuit, main circuit imm_gen
module imm_gen (
  input  [31:0] inst,
  input  [2:0] ImmSel,
  output [31:0] imm
);

  wire [31:0] csr_type, i_type, s_type, sb_type, uj_type;

  assign i_type = {{20{inst[31]}}, inst[31:20]};  // Bit_Extender bit_extender_1
  assign s_type = {{20{inst[31]}}, {inst[31:25], inst[11:7]}};  // Bit_Extender bit_extender_2
  assign sb_type = {{19{inst[31]}}, {inst[31], inst[7], inst[30:25], inst[11:8], 1'b0}};  // Bit_Extender bit_extender_3
  assign uj_type = {{11{inst[31]}}, {inst[31], inst[19:12], inst[20], inst[30:21], 1'b0}};  // Bit_Extender bit_extender_4
  assign csr_type = {{27{1'b0}}, inst[19:15]};  // Bit_Extender bit_extender_5
  Multiplexer #(.enable("false"), .select(3), .width(32)) multiplexer_1 (
    .in0(i_type), .in1(s_type), .in2(sb_type), .in3({inst[31:12], {12{1'b0}}}), .in4(uj_type),
    .in5(csr_type), .out(imm), .sel(ImmSel));  // open: in6, in7

  // Other names for the same wires on the sheet: u_type[31:12] = inst[31:12]

  // Notes on the sheet:
  //   INPUTS to your circuit
  //   DON'T CHANGE THE LOCATIONS OF THE INPUTS AND OUTPUTS!
  //   OUTPUT from your circuit
endmodule
